# Fritzing sketch FullsizeMMVer1 (saved by Fritzing 0.9.4)
breadboards: 1

parts:
  Part1 = Arduino Micro (Rev3)
  VCC1 = Battery block 9V
  M2 = Stepper Motor - Bipolar
  Pololu_A1 = Pololu A4988 [package=SO16]
  Pololu_A2 = Pololu A4988 [package=SO16]
  M3 = Stepper Motor - Bipolar

nets:
  N1: Part1.VIN, VCC1.+
  N2: Part1.GND, VCC1.-
  N3: M2.A, Pololu_A1.2B
  N4: M2.C, Pololu_A1.1B
  N5: M2.B, Pololu_A1.2A
  N6: M2.D, Pololu_A1.1A
  GND: Pololu_A1.GND, Pololu_A2.GND
  N7: Pololu_A2.1B, M3.C
  N8: Pololu_A2.1A, M3.D
  N9: Pololu_A2.2A, M3.B
  N10: Pololu_A2.2B, M3.A
